// Logisim project Comparateur_BinaineParallèle.circ as structural Verilog
// 1
module Comparateur_8_bits (
  input  [7:0] in_1,
  input  Enable,
  input  [7:0] B,
  input  [7:0] C,
  output out_5,
  output out_6,
  output out_7,
  output out_8,
  output out_9,
  output out_10,
  output out_11,
  output out_12,
  output out_13
);

  wire and_1_out, and_2_out, and_5_out, and_6_out, and_9_out, and_10_out, bitselector_1_out,
       bitselector_2_out, bitselector_3_out, Horloge_out, not_1_out, not_2_out, not_3_out, not_4_out,
       not_5_out, not_6_out;
  wire [2:0] counter_1_q, counter_2_q, counter_3_q;

  Clock Horloge (.out(Horloge_out));
  Counter #(.width(3), .max('h7)) counter_1 (
    .Q(counter_1_q), .clk(Horloge_out), .clr(Enable));  // open: load, D, count, carry
  Counter #(.width(3), .max('h7)) counter_2 (
    .Q(counter_2_q), .clk(Horloge_out), .clr(Enable));  // open: load, D, count, carry
  Counter #(.width(3), .max('h7)) counter_3 (
    .Q(counter_3_q), .clk(Horloge_out), .clr(Enable));  // open: load, D, count, carry
  BitSelector bitselector_1 (.in(in_1), .out(bitselector_1_out), .sel(counter_1_q));
  BitSelector bitselector_2 (.in(B), .out(bitselector_2_out), .sel(counter_2_q));
  BitSelector bitselector_3 (.in(C), .out(bitselector_3_out), .sel(counter_3_q));
  not not_1 (not_1_out, bitselector_1_out);
  not not_2 (not_2_out, bitselector_2_out);
  not not_3 (not_3_out, bitselector_1_out);
  not not_4 (not_4_out, bitselector_3_out);
  not not_5 (not_5_out, bitselector_2_out);
  not not_6 (not_6_out, bitselector_3_out);
  and and_1 (and_1_out, bitselector_1_out, bitselector_2_out);
  and and_2 (and_2_out, not_1_out, not_2_out);
  and and_3 (out_6, bitselector_1_out, not_2_out);
  and and_4 (out_7, bitselector_2_out, not_1_out);
  and and_5 (and_5_out, bitselector_1_out, bitselector_3_out);
  and and_6 (and_6_out, not_3_out, not_4_out);
  and and_7 (out_9, bitselector_1_out, not_4_out);
  and and_8 (out_10, bitselector_3_out, not_3_out);
  and and_9 (and_9_out, bitselector_2_out, bitselector_3_out);
  and and_10 (and_10_out, not_5_out, not_6_out);
  and and_11 (out_12, bitselector_2_out, not_6_out);
  and and_12 (out_13, bitselector_3_out, not_5_out);
  or or_1 (out_5, and_1_out, and_2_out);
  or or_2 (out_8, and_5_out, and_6_out);
  or or_3 (out_11, and_9_out, and_10_out);
  LED led_1 (.in(out_5));
  LED led_2 (.in(out_8));
  LED led_3 (.in(out_11));
  LED led_4 (.in(out_6));
  LED led_5 (.in(out_9));
  LED led_6 (.in(out_12));
  LED led_7 (.in(out_7));
  LED led_8 (.in(out_10));
  LED led_9 (.in(out_13));

  // Notes on the sheet:
  //   A
  //   Qi
  //   Qi
  //   Qi
  //   Projet Personnel VHDLxLogisimxModelsim: Comparateur parallèle 3 entrées de 8 bits et 9 sorties de 1 bit. Par Elhadji FALL Licence 2 EEA UHA 2025/2026
  //   "Ai=Bi"
  //   "Ai=Ci"
  //   "Bi=Ci"
  //   "Ai>Bi"
  //   "Ai>Ci"
  //   "Bi>Ci"
  //   "Ai<Bi"
  //   "Ai<Ci"
  //   "Bi<Ci"
endmodule
